// Logisim project CPU.circ as structural Verilog: 8 circuits, main circuit main
module main (
);

  wire BFCORE_ctn, BFCORE_nffw, BFCORE_ninp, BFCORE_outp, BFCORE_pop, BFCORE_push, BFCORE_rlp, BFCORE_wcva,
       CELLWIDTH_sw1, CELLWIDTH_sw2, CHIPSET_kclk, CHIPSET_tclk, CLK_clk, CLK_fst, CLK_full, CLK_snd,
       FSTACK_ffwo, INTERFACE_out_7, INTERFACE_out_8, INTERFACE_out_9, INTERFACE_out_10, INTERFACE_out_11,
       keyboard_1_avail;
  wire [2:0] PROGRAM_data;
  wire [6:0] CHIPSET_tout, keyboard_1_data;
  wire [15:0] bit_extender_1_out;
  wire [31:0] BFCORE_cnoo, BFCORE_cvao, CHIPSET_inpo, FSTACK_pco, MEM_cnoo, MEM_cvao;

  DoubleClock CLK (.FULL(CLK_full), .FST(CLK_fst), .SND(CLK_snd), .CLK(CLK_clk));
  Stack FSTACK (
    .NFFW(INTERFACE_out_11), .POP(INTERFACE_out_9), .PUSH(INTERFACE_out_8), .CLK(CLK_clk), .FULL(CLK_full),
    .CTN(INTERFACE_out_7), .RLP(INTERFACE_out_10), .FST(CLK_fst), .SND(CLK_snd), .FFWO(FSTACK_ffwo),
    .PCO(FSTACK_pco));
  CSI INTERFACE (
    .in_1(CLK_fst), .in_3(BFCORE_push), .in_4(BFCORE_pop), .in_5(BFCORE_rlp), .in_6(BFCORE_nffw),
    .in_2(BFCORE_ctn), .out_8(INTERFACE_out_8), .out_9(INTERFACE_out_9), .out_10(INTERFACE_out_10),
    .out_11(INTERFACE_out_11), .out_7(INTERFACE_out_7));
  Core BFCORE (
    .INP(CHIPSET_inpo), .FFWI(FSTACK_ffwo), .CVAI(MEM_cvao), .INTR(PROGRAM_data), .CNOI(MEM_cnoo),
    .PUSH(BFCORE_push), .CTN(BFCORE_ctn), .NFFW(BFCORE_nffw), .POP(BFCORE_pop), .RLP(BFCORE_rlp),
    .OUTP(BFCORE_outp), .WCVA(BFCORE_wcva), .CVAO(BFCORE_cvao), .CNOO(BFCORE_cnoo), .NINP(BFCORE_ninp));
  Memory MEM (
    .CLK(CLK_clk), .FST(CLK_fst), .SND(CLK_snd), .CNOI(BFCORE_cnoo), .CVAI(BFCORE_cvao), .WCVA(BFCORE_wcva),
    .E16(CELLWIDTH_sw1), .E32(CELLWIDTH_sw2), .CNOO(MEM_cnoo), .CVAO(MEM_cvao));
  DipSwitch #(.number(2)) CELLWIDTH (.sw1(CELLWIDTH_sw1), .sw2(CELLWIDTH_sw2));
  IO CHIPSET (
    .OUTP(BFCORE_outp), .CVA(BFCORE_cvao), .INPEX(keyboard_1_avail), .FULL(CLK_full), .INPI(keyboard_1_data),
    .NINP(BFCORE_ninp), .TCLK(CHIPSET_tclk), .INPO(CHIPSET_inpo), .KCLK(CHIPSET_kclk), .TOUT(CHIPSET_tout));
  ROM #(.addrWidth(16), .dataWidth(3)) PROGRAM (.addr(bit_extender_1_out), .data(PROGRAM_data));
  Bit_Extender #(.in_width(32), .\type ("zero")) bit_extender_1 (.in(FSTACK_pco), .out(bit_extender_1_out));
  TTY #(.cols(80), .rows(24), .trigger("falling")) tty_1 (.data(CHIPSET_tout), .clk(CHIPSET_tclk));  // open: we, clr
  Keyboard #(.trigger("falling")) keyboard_1 (
    .clk(CHIPSET_kclk), .avail(keyboard_1_avail), .data(keyboard_1_data));  // open: re, clr
endmodule

module Memory (
  input  [31:0] CNOI,
  input  CLK,
  input  FST,
  input  WCVA,
  input  SND,
  input  [31:0] CVAI,
  input  E16,
  input  E32,
  output [31:0] CNOO,
  output [31:0] CVAO
);

  wire and_1_out, not_1_out;
  wire [15:0] bit_extender_1_out;
  wire [31:0] MEMORY_dout, multiplexer_1_out, WIDTH_outp;

  Multiplexer #(.width(32)) multiplexer_1 (.in0(CNOO), .in1(CNOI), .out(multiplexer_1_out), .sel(not_1_out));
  not not_1 (not_1_out, FST);
  Register #(.width(32)) register_1 (.D(multiplexer_1_out), .Q(CNOO), .clk(SND));  // open: en, clr
  CellWidth WIDTH (.INP(CVAI), .E32(E32), .E16(E16), .OUTP(WIDTH_outp));
  Bit_Extender #(.in_width(32), .\type ("zero")) bit_extender_1 (.in(CNOO), .out(bit_extender_1_out));
  and and_1 (and_1_out, WCVA, SND);
  RAM #(.addrWidth(16), .dataWidth(32), .trigger("falling")) MEMORY (
    .addr(bit_extender_1_out), .we(and_1_out), .oe(FST), .clk(CLK), .din(WIDTH_outp), .dout(MEMORY_dout));
  Register #(.width(32)) register_2 (.D(MEMORY_dout), .Q(CVAO), .clk(SND));  // open: en, clr
endmodule

module CSI (
  input  in_1,
  input  in_2,
  input  in_3,
  input  in_4,
  input  in_5,
  input  in_6,
  output out_7,
  output out_8,
  output out_9,
  output out_10,
  output out_11
);

  Register #(.width(1)) register_1 (.D(in_2), .Q(out_7), .clk(in_1));  // open: en, clr
  Register #(.width(1)) register_2 (.D(in_3), .Q(out_8), .clk(in_1));  // open: en, clr
  Register #(.width(1)) register_3 (.D(in_4), .Q(out_9), .clk(in_1));  // open: en, clr
  Register #(.width(1)) register_4 (.D(in_5), .Q(out_10), .clk(in_1));  // open: en, clr
  Register #(.width(1)) register_5 (.D(in_6), .Q(out_11), .clk(in_1));  // open: en, clr
endmodule

module Stack (
  input  NFFW,
  input  FULL,
  input  CTN,
  input  RLP,
  input  POP,
  input  PUSH,
  input  FST,
  input  SND,
  input  CLK,
  output FFWO,
  output [31:0] PCO
);

  wire and_1_out, and_5_out, comparator_1_eq, multiplexer_6_out, nor_1_out, or_1_out, or_2_out, or_3_out;
  wire [0:0] or_4_out;
  wire [1:0] and_2_out;
  wire [1:1] and_4_out;
  wire [7:0] adder_1_out, multiplexer_1_out, multiplexer_2_out, multiplexer_3_out, multiplexer_4_out,
       multiplexer_5_out, SP_q, SPBFF_q, subtractor_1_out;
  wire [31:0] adder_2_out, multiplexer_7_out, multiplexer_8_out, multiplexer_9_out, STACK_dout;

  or or_1 (or_1_out, PUSH, POP);
  Multiplexer #(.select(2), .width(8)) multiplexer_1 (
    .in0(SPBFF_q), .in1(multiplexer_2_out), .in2({8{1'b0}}), .out(multiplexer_1_out),
    .sel({and_4_out[1], NFFW}));  // open: in3
  Multiplexer #(.width(8)) multiplexer_2 (.in0(SP_q), .in1(multiplexer_3_out), .out(multiplexer_2_out), .sel(FST));
  Register #(.trigger("falling")) SPBFF (.D(multiplexer_1_out), .Q(SPBFF_q), .clk(SND));  // open: en, clr
  Register SP (.D(multiplexer_2_out), .Q(SP_q), .clk(SND));  // open: en, clr
  Multiplexer #(.select(2), .width(8)) multiplexer_3 (
    .in0(SP_q), .in1(adder_1_out), .in2(subtractor_1_out), .out(multiplexer_3_out), .sel({POP, PUSH}));  // open: in3
  Multiplexer #(.width(8)) multiplexer_4 (.in0(SP_q), .in1(adder_1_out), .out(multiplexer_4_out), .sel(SND));
  and and_1 (and_1_out, SND, or_1_out);
  Comparator #(.mode("unsigned")) comparator_1 (
    .a(SPBFF_q), .b(multiplexer_4_out), .eq(comparator_1_eq));  // open: gt, lt
  Adder adder_1 (.a(SP_q), .b(8'h1), .out(adder_1_out));  // open: cin, cout
  Subtractor subtractor_1 (.a(SP_q), .b(8'h1), .out(subtractor_1_out));  // open: bin, bout
  Multiplexer #(.select(2), .width(8)) multiplexer_5 (
    .in0(SP_q), .in1(adder_1_out), .in2(subtractor_1_out), .out(multiplexer_5_out), .sel(and_2_out));  // open: in3
  or or_2 (or_2_out, NFFW, multiplexer_6_out);
  Multiplexer multiplexer_6 (.in0(FFWO), .in1(1'b0), .out(multiplexer_6_out), .sel(and_4_out[1]));
  and and_2 (and_2_out[0], POP, or_3_out);
  and and_3 (and_2_out[1], POP, FST);
  RAM #(.dataWidth(32), .trigger("falling")) STACK (
    .addr(multiplexer_5_out), .we(and_1_out), .oe(FST), .clk(CLK), .din(multiplexer_7_out), .dout(STACK_dout));
  and and_4 (and_4_out[1], and_5_out, FULL);
  and and_5 (and_5_out, comparator_1_eq, POP);
  or or_3 (or_3_out, SND, nor_1_out);
  Register #(.width(1)) FFW (.D(or_2_out), .Q(FFWO), .clk(SND));  // open: en, clr
  or or_4 (or_4_out[0], CTN, POP, PUSH);
  nor nor_1 (nor_1_out, SND, FST);
  Multiplexer #(.width(32)) multiplexer_7 (.in0(PCO), .in1({32{1'b0}}), .out(multiplexer_7_out), .sel(and_2_out[0]));
  Register #(.width(32)) PC (.D(multiplexer_8_out), .Q(PCO), .clk(SND));  // open: en, clr
  Multiplexer #(.width(32)) multiplexer_8 (.in0(PCO), .in1(multiplexer_9_out), .out(multiplexer_8_out), .sel(FST));
  Multiplexer #(.select(2), .width(32)) multiplexer_9 (
    .in0(PCO), .in1(adder_2_out), .in2(STACK_dout), .out(multiplexer_9_out), .sel({RLP, or_4_out[0]}));  // open: in3
  Adder #(.width(32)) adder_2 (.a(PCO), .b(32'h1), .out(adder_2_out));  // open: cin, cout

  // Notes on the sheet:
  //   PUSH
  //   POP
  //   POP
endmodule

module Core (
  input  [31:0] CVAI,
  input  [31:0] CNOI,
  input  [2:0] INTR,
  input  [31:0] INP,
  input  FFWI,
  output PUSH,
  output CTN,
  output POP,
  output RLP,
  output WCVA,
  output [31:0] CNOO,
  output NFFW,
  output OUTP,
  output [31:0] CVAO,
  output NINP
);

  wire and_1_out, and_7_out, and_8_out, comparator_1_eq, comparator_2_eq, decoder_1_out0, decoder_1_out1,
       decoder_1_out2, decoder_1_out3, decoder_1_out4, decoder_1_out5, decoder_1_out7, not_1_out, not_2_out,
       not_3_out, or_1_out, or_2_out, or_3_out, or_4_out;
  wire [31:0] adder_1_out, multiplexer_1_out, multiplexer_3_out, multiplexer_4_out, subtractor_1_out;

  Decoder #(.enable("false"), .select(3)) decoder_1 (
    .out0(decoder_1_out0), .out1(decoder_1_out1), .out2(decoder_1_out2), .out3(decoder_1_out3),
    .out4(decoder_1_out4), .out5(decoder_1_out5), .out6(PUSH), .out7(decoder_1_out7), .sel(INTR));
  nor nor_1 (CTN, decoder_1_out7, PUSH);
  Comparator #(.mode("unsigned"), .width(32)) comparator_1 (
    .a(CVAI), .b({32{1'b0}}), .eq(comparator_1_eq));  // open: gt, lt
  and and_1 (and_1_out, PUSH, comparator_1_eq);
  and and_2 (POP, decoder_1_out7, comparator_1_eq);
  and and_3 (NFFW, and_1_out, not_2_out);
  or or_1 (or_1_out, decoder_1_out0, decoder_1_out1);
  or or_2 (or_2_out, decoder_1_out2, decoder_1_out3);
  or or_3 (or_3_out, decoder_1_out1, decoder_1_out3);
  not not_1 (not_1_out, comparator_1_eq);
  and and_4 (RLP, decoder_1_out7, not_1_out);
  or or_4 (or_4_out, NINP, or_2_out);
  and and_5 (WCVA, or_4_out, not_2_out);
  and and_6 (OUTP, decoder_1_out4, not_2_out);
  and and_7 (and_7_out, or_4_out, not_2_out);
  not not_2 (not_2_out, FFWI);
  Multiplexer #(.width(32)) multiplexer_1 (
    .in0(CVAI), .in1(multiplexer_4_out), .out(multiplexer_1_out), .sel(and_7_out));
  Multiplexer #(.width(32)) multiplexer_2 (.in0(multiplexer_1_out), .in1(INP), .out(CVAO), .sel(NINP));
  Multiplexer #(.width(32)) multiplexer_3 (.in0(CVAI), .in1(CNOI), .out(multiplexer_3_out), .sel(or_1_out));
  Adder #(.width(32)) adder_1 (.a(multiplexer_3_out), .b(32'h1), .out(adder_1_out));  // open: cin, cout
  Multiplexer #(.width(32)) multiplexer_4 (
    .in0(adder_1_out), .in1(subtractor_1_out), .out(multiplexer_4_out), .sel(or_3_out));
  and and_8 (and_8_out, or_1_out, not_2_out);
  Subtractor #(.width(32)) subtractor_1 (.a(multiplexer_3_out), .b(32'h1), .out(subtractor_1_out));  // open: bin, bout
  Multiplexer #(.width(32)) multiplexer_5 (.in0(CNOI), .in1(multiplexer_4_out), .out(CNOO), .sel(and_8_out));
  and and_9 (NINP, not_3_out, decoder_1_out5);
  Comparator #(.mode("unsigned"), .width(32)) comparator_2 (
    .a({32{1'b0}}), .b(INP), .eq(comparator_2_eq));  // open: gt, lt
  not not_3 (not_3_out, comparator_2_eq);

  // Notes on the sheet:
  //   R/W = NO
  //   R/W = VA
  //   ADD / SUB
endmodule

module DoubleClock (
  output FST,
  output SND,
  output CLK,
  output FULL
);

  wire and_1_out, not_1_out, or_1_out, t_ff_1_q, t_ff_1_qn;

  Clock clock_1 (.out(CLK));
  T_Flip_Flop t_ff_1 (.clk(CLK), .T(CLK), .Q(t_ff_1_q), .Qn(t_ff_1_qn));  // open: preset, reset
  not not_1 (not_1_out, CLK);
  and and_1 (and_1_out, not_1_out, t_ff_1_q);
  and and_2 (FST, CLK, t_ff_1_q);
  and and_3 (SND, t_ff_1_qn, CLK);
  or or_1 (or_1_out, SND, FST);
  or or_2 (FULL, and_1_out, or_1_out);
endmodule

module IO (
  input  FULL,
  input  OUTP,
  input  [31:0] CVA,
  input  NINP,
  input  INPEX,
  input  [6:0] INPI,
  output TCLK,
  output [6:0] TOUT,
  output KCLK,
  output [31:0] INPO
);

  wire comparator_1_eq, not_1_out;
  wire [6:0] bit_extender_1_out, multiplexer_1_out;

  not not_1 (not_1_out, FULL);
  and and_1 (TCLK, not_1_out, OUTP);
  Bit_Extender #(.in_width(32), .out_width(7), .\type ("zero")) bit_extender_1 (.in(CVA), .out(bit_extender_1_out));
  Multiplexer #(.width(7)) multiplexer_1 (.in0({7{1'b0}}), .in1(INPI), .out(multiplexer_1_out), .sel(INPEX));
  Comparator #(.mode("unsigned"), .width(7)) comparator_1 (
    .a(bit_extender_1_out), .b(7'b0001001), .eq(comparator_1_eq));  // open: gt, lt
  assign INPO = {{25{1'b0}}, multiplexer_1_out};  // Bit_Extender bit_extender_2
  and and_2 (KCLK, not_1_out, NINP, INPEX);
  Multiplexer #(.width(7)) multiplexer_2 (
    .in0(bit_extender_1_out), .in1(7'b0100000), .out(TOUT), .sel(comparator_1_eq));
endmodule

module CellWidth (
  input  [31:0] INP,
  input  E32,
  input  E16,
  output [31:0] OUTP
);

  wire or_1_out;

  Multiplexer #(.width(8)) multiplexer_1 (.in0({8{1'b0}}), .in1(INP[15:8]), .out(OUTP[15:8]), .sel(or_1_out));
  or or_1 (or_1_out, E16, E32);
  Multiplexer #(.width(8)) multiplexer_2 (.in0({8{1'b0}}), .in1(INP[23:16]), .out(OUTP[23:16]), .sel(E32));
  Multiplexer #(.width(8)) multiplexer_3 (.in0({8{1'b0}}), .in1(INP[31:24]), .out(OUTP[31:24]), .sel(E32));

  assign OUTP[7:0] = INP[7:0];
endmodule
